// Logisim project fsm_1_2_switch.circ as structural Verilog: 1 circuit, main circuit main
module main (
);

  wire button_1_out, button_2_out, clock_1_out, d_ff_1_q;

  Button button_1 (.out(button_1_out));
  Button button_2 (.out(button_2_out));
  Clock clock_1 (.out(clock_1_out));
  D_Flip_Flop d_ff_1 (.clk(clock_1_out), .Q(d_ff_1_q));  // open: D, Qn, preset, reset
  LED led_1 (.in(d_ff_1_q));

  // Notes on the sheet:
  //   A
  //   B
endmodule
